// Logisim project FSM.circ as structural Verilog: 10 circuits, main circuit FSM
module FSM (
  input  FSM_Input,
  output out_2
);

  wire clock_1_out;
  wire [1:0] fsmlogic_1_next_state, register_1_q;

  Register #(.width(2)) register_1 (.D(fsmlogic_1_next_state), .clk(clock_1_out), .Q(register_1_q));  // open: en, clr
  Clock clock_1 (.out(clock_1_out));
  FSMLogic fsmlogic_1 (
    .Input_Bit(FSM_Input), .Current_State(register_1_q), .Output(out_2), .Next_State(fsmlogic_1_next_state));
endmodule

// FSM Logic
module FSMLogic (
  input  Input_Bit,
  input  [1:0] Current_State,
  output Output,
  output [1:0] Next_State
);

  wire and_1_out, and_2_out, not_1_out, not_2_out, not_3_out;

  not not_1 (not_1_out, Current_State[1]);
  not not_2 (not_2_out, Input_Bit);
  not not_3 (not_3_out, Current_State[0]);
  and and_1 (and_1_out, Input_Bit, not_1_out);
  or or_1 (Output, and_1_out, and_2_out);
  and and_2 (and_2_out, not_2_out, not_3_out);
  StateBitZero statebitzero_1 (
    .Input(Input_Bit), .State_Bit_0(Current_State[0]), .State_Bit_1(Current_State[1]),
    .New_State_0(Next_State[0]));
  StateBitOne statebitone_1 (
    .Input(Input_Bit), .State_Bit_0(Current_State[0]), .State_Bit_1(Current_State[1]),
    .New_State_1(Next_State[1]));

  // Other names for the same wires on the sheet: Currrent_State_0 = Current_State[0];
  //   Current_State_1 = Current_State[1]
endmodule

// State Bit 1
module StateBitOne (
  input  Input,
  input  State_Bit_0,
  input  State_Bit_1,
  output New_State_1
);

  // NOT_Gate not_1 has open pins: in=Input, out=open
  // NOT_Gate not_2 has open pins: in=State_Bit_0, out=open
  // NOT_Gate not_3 has open pins: in=State_Bit_1, out=open
  or or_1 (New_State_1, Input, State_Bit_0);

  // Notes on the sheet:
  //   PUT CIRCUITRY HERE
endmodule

// State Bit 0
module StateBitZero (
  input  Input,
  input  State_Bit_0,
  input  State_Bit_1,
  output New_State_0
);

  wire not_1_out;

  not not_1 (not_1_out, Input);
  // NOT_Gate not_2 has open pins: in=State_Bit_0, out=open
  // NOT_Gate not_3 has open pins: in=State_Bit_1, out=open
  or or_1 (New_State_0, not_1_out, State_Bit_1);

  // Notes on the sheet:
  //   PUT CIRCUITRY HERE
endmodule

module Ex4 (
  input  [7:0] In1,
  output Out1,
  output [7:0] Out2
);

  not not_1 (Out2[7], In1[7]);
  and and_1 (Out1, In1[0], In1[7]);

  assign Out2[6:0] = In1[6:0];
endmodule

module rotr (
  input  [15:0] A,
  input  [3:0] B,
  output [15:0] out_3
);

  wire [15:0] multiplexer_1_out, multiplexer_2_out, multiplexer_3_out, rot1_1_out1, rot2_1_out2, rot4_1_out4,
       rot8_1_out8;

  rot1 rot1_1 (.In1(A), .Out1(rot1_1_out1));
  Multiplexer #(.width(16), .enable("false")) multiplexer_1 (
    .in0(A), .in1(rot1_1_out1), .out(multiplexer_1_out), .sel(B[0]));
  rot2 rot2_1 (.In2(multiplexer_1_out), .Out2(rot2_1_out2));
  Multiplexer #(.width(16), .enable("false")) multiplexer_2 (
    .in0(multiplexer_1_out), .in1(rot2_1_out2), .out(multiplexer_2_out), .sel(B[1]));
  rot4 rot4_1 (.In4(multiplexer_2_out), .Out4(rot4_1_out4));
  Multiplexer #(.width(16), .enable("false")) multiplexer_3 (
    .in0(multiplexer_2_out), .in1(rot4_1_out4), .out(multiplexer_3_out), .sel(B[2]));
  rot8 rot8_1 (.In8(multiplexer_3_out), .Out8(rot8_1_out8));
  Multiplexer #(.width(16), .enable("false")) multiplexer_4 (
    .in0(multiplexer_3_out), .in1(rot8_1_out8), .out(out_3), .sel(B[3]));
endmodule

module rot1 (
  input  [15:0] In1,
  output [15:0] Out1
);


  assign Out1 = {In1[14:0], In1[15]};
endmodule

module rot2 (
  input  [15:0] In2,
  output [15:0] Out2
);

  wire [15:0] rot1_1_out1;

  rot1 rot1_1 (.In1(In2), .Out1(rot1_1_out1));
  rot1 rot1_2 (.In1(rot1_1_out1), .Out1(Out2));
endmodule

module rot4 (
  input  [15:0] In4,
  output [15:0] Out4
);

  wire [15:0] rot2_1_out2;

  rot2 rot2_1 (.In2(In4), .Out2(rot2_1_out2));
  rot2 rot2_2 (.In2(rot2_1_out2), .Out2(Out4));
endmodule

module rot8 (
  input  [15:0] In8,
  output [15:0] Out8
);

  wire [15:0] rot4_1_out4;

  rot4 rot4_1 (.In4(In8), .Out4(rot4_1_out4));
  rot4 rot4_2 (.In4(rot4_1_out4), .Out4(Out8));
endmodule
