// Logisim project alu.circ as structural Verilog: 2 circuits, main circuit alu
module alu (
  input  [31:0] A,
  input  [31:0] B,
  input  [3:0] ALUSel,
  output [31:0] Result
);

  wire comparator_1_lt;
  wire [1:0] Oput;
  wire [4:0] bit_extender_1_out, bit_extender_2_out, bit_extender_3_out;
  wire [31:0] ADD1, AND1, ANegMul, BNegMul, DIV1, DNeg, MUL1, MULH1, MULHU1, multiplier_3_cout,
       multiplier_4_cout, negator_1_out, negator_2_out, negator_3_out, negator_4_out, OR1, REMU1, SLL1, SLT1,
       SRA1, SRL1, SUB1, XOR1;

  Bit_Extender #(.in_width(32), .out_width(5), .\type ("zero")) bit_extender_1 (.in(B), .out(bit_extender_1_out));
  Bit_Extender #(.in_width(32), .out_width(5)) bit_extender_2 (.in(B), .out(bit_extender_2_out));
  Bit_Extender #(.in_width(32), .out_width(5), .\type ("zero")) bit_extender_3 (.in(B), .out(bit_extender_3_out));
  Negator #(.width(32)) negator_1 (.in(A), .out(negator_1_out));
  Negator #(.width(32)) negator_2 (.in(B), .out(negator_2_out));
  Negator #(.width(32)) negator_3 (.in(A), .out(negator_3_out));
  Adder #(.width(32)) adder_1 (.a(A), .b(B), .out(ADD1));  // open: cin, cout
  assign AND1 = A & B;  // AND_Gate and_1, 32 bits wide
  assign OR1 = A | B;  // OR_Gate or_1, 32 bits wide
  assign XOR1 = A ^ B;  // XOR_Gate xor_1, 32 bits wide
  Shifter #(.width(32), .shift("lr")) shifter_1 (.in(A), .\dist (bit_extender_1_out), .out(SRL1));
  Shifter #(.width(32), .shift("ar")) shifter_2 (.in(A), .\dist (bit_extender_2_out), .out(SRA1));
  Shifter #(.width(32)) shifter_3 (.in(A), .\dist (bit_extender_3_out), .out(SLL1));
  Comparator #(.width(32)) comparator_1 (.a(A), .b(B), .lt(comparator_1_lt));  // open: gt, eq
  Divider #(.width(32)) divider_1 (.a(A), .b(B), .out(DIV1));  // open: upper, rem
  Divider #(.width(32)) divider_2 (.a(A), .b(B), .rem(REMU1));  // open: out, upper
  Multiplier #(.width(32)) multiplier_1 (.a(A), .b(B), .out(MUL1));  // open: cin, cout
  Multiplier #(.width(32)) multiplier_2 (.a(A), .b(B), .cout(MULHU1));  // open: out, cin
  Subtractor #(.width(32)) subtractor_1 (.a(A), .b(B), .out(SUB1));  // open: bin, bout
  isNeg isneg_1 (.in_1(A), .out_2(Oput[0]));
  isNeg isneg_2 (.in_1(B), .out_2(Oput[1]));
  Multiplier #(.width(32)) multiplier_3 (.a(negator_1_out), .b(B), .cout(multiplier_3_cout));  // open: out, cin
  Multiplier #(.width(32)) multiplier_4 (.a(negator_2_out), .b(A), .cout(multiplier_4_cout));  // open: out, cin
  Multiplier #(.width(32)) multiplier_5 (.a(negator_3_out), .b(negator_4_out), .cout(DNeg));  // open: out, cin
  Negator #(.width(32)) negator_4 (.in(B), .out(negator_4_out));
  assign SLT1 = {{31{1'b0}}, comparator_1_lt};  // Bit_Extender bit_extender_4
  Negator #(.width(32)) negator_5 (.in(multiplier_3_cout), .out(ANegMul));
  Negator #(.width(32)) negator_6 (.in(multiplier_4_cout), .out(BNegMul));
  Multiplexer #(.select(2), .width(32), .enable("false")) multiplexer_1 (
    .in0(MULHU1), .in1(ANegMul), .in2(BNegMul), .in3(DNeg), .out(MULH1), .sel(Oput));
  Multiplexer #(.select(4), .width(32), .enable("false")) multiplexer_2 (
    .in0(ADD1), .in1(AND1), .in2(OR1), .in3(XOR1), .in4(SRL1), .in5(SRA1), .in6(SLL1), .in7(SLT1),
    .in8(DIV1), .in9(REMU1), .in10(MUL1), .in11(MULHU1), .in12(SUB1), .in13(B), .in14(MULH1), .out(Result),
    .sel(ALUSel));  // open: in15

  // Other names for the same wires on the sheet: posMul[31:0] = MULHU1

  // Notes on the sheet:
  //   INPUTS to your circuit
  //   DON'T CHANGE THE LOCATIONS OF THE INPUTS AND OUTPUTS!
  //   OUTPUT from your circuit
endmodule

module isNeg (
  input  [31:0] in_1,
  output out_2
);


  assign out_2 = in_1[31];
endmodule
