// Logisim project cpu.circ as structural Verilog: 6 circuits, main circuit main
module main (
  input  [31:0] INSTRUCTION,
  input  CLOCK,
  output [31:0] FETCH_ADDRESS,
  output [31:0] ra,
  output [31:0] sp,
  output [31:0] t0,
  output [31:0] t1,
  output [31:0] t2,
  output [31:0] s0,
  output [31:0] s1,
  output [31:0] a0
);

  wire ASel, BrEq, BrLt, BrUn, BSel, DMEM_p1, DMEM_p7, DMEM_p9, DMEM_p12, DMEM_p14, DMEM_p16, MemRW, PCSel,
       RegWEn;
  wire [1:0] WBSel;
  wire [2:0] ImmSel;
  wire [3:0] ALUSel;
  wire [6:0] Next_Instr;
  wire [24:0] ImmPut;
  wire [31:0] adder_1_out, adder_2_out, Alu_Res, DMEM_p11, ImmVal, multiplexer_1_out, multiplexer_2_out,
       prev_PC, RegA, RegB, RegOut1, RegOut2, WB;

  Adder #(.width(32)) adder_1 (.a(FETCH_ADDRESS), .b(32'h4), .out(adder_1_out));  // open: cin, cout
  Register #(.width(32)) PC (.D(multiplexer_1_out), .clk(CLOCK), .Q(FETCH_ADDRESS));  // open: en, clr
  Multiplexer #(.width(32), .enable("false")) multiplexer_1 (
    .in0(adder_1_out), .in1(Alu_Res), .out(multiplexer_1_out), .sel(PCSel));
  Control Control_Unit (
    .INSTRS({ImmPut, Next_Instr}), .BrEq(BrEq), .BrLt(BrLt), .PCSel(PCSel), .RegWEn(RegWEn), .ImmSel(ImmSel),
    .BrUn(BrUn), .ASel(ASel), .BSel(BSel), .ALUSel(ALUSel), .MemRW(MemRW), .WBSel(WBSel));  // open: out_13
  BrComp Branch_Comparator (.RegOut1(RegOut1), .RegOut2(RegOut2), .BrUn(BrUn), .BrEq(BrEq), .BrLt(BrLt));
  alu Arithmetic_Logic_Unit (.A(RegA), .B(RegB), .ALUSel(ALUSel), .Result(Alu_Res));
  ImmGen Imm_Gen (.ImmPut(ImmPut), .ImmSel(ImmSel), .INstr({ImmPut, Next_Instr}), .out_4(ImmVal));
  SelA A_Sel (.PC_Val(prev_PC), .RS_1(RegOut1), .ASel_IN(ASel), .SelA_Val(RegA));
  SelB Sel_B (.Reg2_Val(RegOut2), .Imm_Val(ImmVal), .BSel_In(BSel), .SelB_out(RegB));
  Register #(.width(32)) register_1 (.D(multiplexer_2_out), .clk(CLOCK), .Q({ImmPut, Next_Instr}));  // open: en, clr
  Multiplexer #(.width(32), .enable("false")) multiplexer_2 (
    .in0(INSTRUCTION), .in1({32{1'b0}}), .out(multiplexer_2_out), .sel(PCSel));
  Register #(.width(32)) register_2 (.D(FETCH_ADDRESS), .clk(CLOCK), .Q(prev_PC));  // open: en, clr
  regfile_main RegFile (
    .rs2(ImmPut[17:13]), .rd(ImmPut[4:0]), .Read_Data_1(RegOut1), .Read_Data_2(RegOut2), .ra(ra), .sp(sp),
    .t0(t0), .t1(t1), .t2(t2), .s0(s0), .s1(s1), .a0(a0), .rs1(ImmPut[12:8]), .Write_Data(WB),
    .RegWEn(RegWEn), .clk(CLOCK));  // open: in_7
  // mem_main DMEM: pin names not known; wires that end beside it: DMEM_p1, DMEM_p1, Alu_Res, RegOut2, MemRW, CLOCK, DMEM_p7, DMEM_p7, DMEM_p9, DMEM_p9, DMEM_p11, DMEM_p12, DMEM_p12, DMEM_p14, DMEM_p14, DMEM_p16
  Adder #(.width(32)) adder_2 (.a(prev_PC), .b(32'h4), .out(adder_2_out));  // open: cin, cout
  Multiplexer #(.select(2), .width(32), .enable("false")) multiplexer_3 (
    .in0(adder_2_out), .in1(Alu_Res), .in2(DMEM_p11), .out(WB), .sel(WBSel));  // open: in3

  // Other names for the same wires on the sheet: clk = CLOCK; Next_Instr[31:7] = ImmPut; retReg[4:0] = ImmPut[4:0];
  //   Reg1[4:0] = ImmPut[12:8]; Reg2[4:0] = ImmPut[17:13]; PROGRAM_COUNTER[31:0] = FETCH_ADDRESS

  // Notes on the sheet:
  //   Output
  //   Inputs/Outputs from run.circ. DO NOT MOVE THESE.
  //   Inputs
  //   It is OK to move the PC, RegFile, ALU, and MEM to wherever is most convenient for you when constructing your CPU, and to delete this text
  //   Inputs/Outputs from run.circ. DO NOT MOVE THESE.
endmodule

module ImmGen (
  input  [24:0] ImmPut,
  input  [2:0] ImmSel,
  input  [31:0] INstr,
  output [31:0] out_4
);

  wire [31:0] bit_extender_1_out, bit_extender_2_out, bit_extender_3_out, bit_extender_4_out;

  assign bit_extender_1_out = {{20{ImmPut[24]}}, ImmPut[24:13]};  // Bit_Extender bit_extender_1
  assign bit_extender_2_out = {{20{ImmPut[24]}}, {ImmPut[24:18], ImmPut[4:0]}};  // Bit_Extender bit_extender_2
  assign bit_extender_3_out = {{19{ImmPut[24]}}, {ImmPut[24], ImmPut[0], ImmPut[23:18], ImmPut[4:1], 1'b0}};  // Bit_Extender bit_extender_3
  assign bit_extender_4_out = {{11{INstr[31]}}, {INstr[31], INstr[19:12], INstr[20], INstr[30:21], 1'b0}};  // Bit_Extender bit_extender_4
  Multiplexer #(.select(3), .width(32), .enable("false")) multiplexer_1 (
    .in1(bit_extender_1_out), .in2(bit_extender_2_out), .in3(bit_extender_3_out),
    .in4({ImmPut[24:5], {12{1'b0}}}), .in5(bit_extender_4_out), .out(out_4), .sel(ImmSel));  // open: in0, in6, in7

  // Other names for the same wires on the sheet: ImmInput[24:0] = ImmPut; Inst[31:0] = INstr; ImmVal[31:0] = out_4
endmodule

module Control (
  input  [31:0] INSTRS,
  input  BrEq,
  input  BrLt,
  output PCSel,
  output RegWEn,
  output [2:0] ImmSel,
  output BrUn,
  output ASel,
  output BSel,
  output [3:0] ALUSel,
  output MemRW,
  output [1:0] WBSel,
  output out_13
);

  wire and_2_out, and_3_out, and_4_out, and_5_out, and_6_out, and_7_out, and_8_out, and_9_out, and_10_out,
       and_11_out, and_12_out, and_13_out, and_14_out, and_15_out, and_16_out, and_17_out, and_18_out,
       and_19_out, and_20_out, and_21_out, and_22_out, and_23_out, and_24_out, and_25_out, and_26_out, BEQ,
       BLT, BNE, f3_0, f3_1, f3_2, f3_3, f3_4, f3_5, f3_6, f3_7, f7_0, f7_0F, f7_1, f7_20, I, JALR,
       not_1_out, or_2_out, or_5_out, or_6_out, or_7_out, or_8_out, or_9_out, or_10_out, or_11_out,
       or_12_out, R, SB, U, UJ;
  wire [2:0] adder_12_out, adder_14_out, adder_15_out, bit_extender_1_out, bit_extender_2_out,
       bit_extender_3_out, bit_extender_4_out, bit_extender_5_out, multiplier_14_out, multiplier_15_out,
       multiplier_16_out, multiplier_17_out, multiplier_18_out;
  wire [3:0] ADD_Sig, adder_1_out, adder_2_out, adder_3_out, adder_4_out, adder_5_out, adder_6_out,
       adder_7_out, adder_8_out, adder_9_out, adder_10_out, adder_11_out, AND_Sig, DIV_Sig, MUL_Sig,
       MULHU_Sig, multiplier_1_out, multiplier_2_out, multiplier_3_out, multiplier_4_out, multiplier_5_out,
       multiplier_6_out, multiplier_7_out, multiplier_8_out, multiplier_9_out, multiplier_10_out,
       multiplier_11_out, multiplier_12_out, multiplier_13_out, OR_Sig, REMU_Sig, SLL_Sig, SLT_Sig, SRA_Sig,
       SRL_Sig, SUB_Sig, XOR_Sig;

  not not_1 (not_1_out, BrEq);
  or or_1 (ASel, SB, UJ);
  not not_2 (BSel, R);
  and and_1 (RegWEn, ~MemRW, ~SB);  // AND_Gate
  or or_2 (or_2_out, JALR, UJ);
  and and_2 (and_2_out, BEQ, SB, BrEq);
  and and_3 (and_3_out, BrLt, BLT, SB);
  and and_4 (and_4_out, BrLt, BrUn, SB);
  and and_5 (and_5_out, BNE, not_1_out, SB);
  or or_3 (WBSel[0], I, R, U);
  Multiplier #(.width(4)) multiplier_1 (.a(ADD_Sig), .b(4'b0000), .out(multiplier_1_out));  // open: cin, cout
  Adder #(.width(4)) adder_1 (.a(multiplier_1_out), .b(multiplier_2_out), .out(adder_1_out));  // open: cin, cout
  Multiplier #(.width(4)) multiplier_2 (.a(AND_Sig), .b(4'b0001), .out(multiplier_2_out));  // open: cin, cout
  Multiplier #(.width(4)) multiplier_3 (.a(OR_Sig), .b(4'b0010), .out(multiplier_3_out));  // open: cin, cout
  or or_4 (PCSel, or_2_out, and_2_out, and_3_out, and_4_out, and_5_out);
  Adder #(.width(4)) adder_2 (.a(adder_1_out), .b(multiplier_3_out), .out(adder_2_out));  // open: cin, cout
  Multiplier #(.width(4)) multiplier_4 (.a(XOR_Sig), .b(4'b0011), .out(multiplier_4_out));  // open: cin, cout
  Multiplier #(.width(4)) multiplier_5 (.a(SRL_Sig), .b(4'b0100), .out(multiplier_5_out));  // open: cin, cout
  Decoder #(.select(3), .enable("false")) decoder_1 (
    .out0(BEQ), .out1(BNE), .out4(BLT), .out6(BrUn), .sel(INSTRS[14:12]));  // open: out2, out3, out5, out7
  Adder #(.width(4)) adder_3 (.a(adder_2_out), .b(multiplier_4_out), .out(adder_3_out));  // open: cin, cout
  Multiplier #(.width(4)) multiplier_6 (.a(SRA_Sig), .b(4'b0101), .out(multiplier_6_out));  // open: cin, cout
  Multiplier #(.width(4)) multiplier_7 (.a(SLL_Sig), .b(4'b0110), .out(multiplier_7_out));  // open: cin, cout
  Multiplier #(.width(4)) multiplier_8 (.a(SLT_Sig), .b(4'b0111), .out(multiplier_8_out));  // open: cin, cout
  Decoder #(.select(5), .enable("false")) decoder_2 (
    .out0(WBSel[1]), .out4(I), .out8(MemRW), .out12(R), .out13(U), .out24(SB), .out25(JALR), .out27(UJ),
    .sel(INSTRS[6:2]));  // open: out1, out2, out3, out5, out6, out7, out9, out10, out11, out14, out15, out16, out17, out18, out19, out20, out21, out22, out23, out26, out28, out29, out30, out31
  Adder #(.width(4)) adder_4 (.a(adder_3_out), .b(multiplier_5_out), .out(adder_4_out));  // open: cin, cout
  Adder #(.width(4)) adder_5 (.a(adder_4_out), .b(multiplier_6_out), .out(adder_5_out));  // open: cin, cout
  Multiplier #(.width(4)) multiplier_9 (.a(DIV_Sig), .b(4'b1000), .out(multiplier_9_out));  // open: cin, cout
  Multiplier #(.width(4)) multiplier_10 (.a(REMU_Sig), .b(4'b1001), .out(multiplier_10_out));  // open: cin, cout
  Multiplier #(.width(4)) multiplier_11 (.a(MUL_Sig), .b(4'b1010), .out(multiplier_11_out));  // open: cin, cout
  Multiplier #(.width(4)) multiplier_12 (.a(MULHU_Sig), .b(4'b1011), .out(multiplier_12_out));  // open: cin, cout
  Adder #(.width(4)) adder_6 (.a(adder_5_out), .b(multiplier_7_out), .out(adder_6_out));  // open: cin, cout
  Multiplier #(.width(4)) multiplier_13 (.a(SUB_Sig), .b(4'b1100), .out(multiplier_13_out));  // open: cin, cout
  Adder #(.width(4)) adder_7 (.a(adder_6_out), .b(multiplier_8_out), .out(adder_7_out));  // open: cin, cout
  Adder #(.width(4)) adder_8 (.a(adder_7_out), .b(multiplier_9_out), .out(adder_8_out));  // open: cin, cout
  Adder #(.width(4)) adder_9 (.a(adder_8_out), .b(multiplier_10_out), .out(adder_9_out));  // open: cin, cout
  or or_5 (or_5_out, WBSel[1], I);
  Decoder #(.select(3), .enable("false")) decoder_3 (
    .out0(f3_0), .out1(f3_1), .out2(f3_2), .out3(f3_3), .out4(f3_4), .out5(f3_5), .out6(f3_6), .out7(f3_7),
    .sel(INSTRS[14:12]));
  Decoder #(.select(3), .enable("false")) decoder_4 (
    .out0(f7_0), .out1(f7_1), .out3(f7_0F), .out4(f7_20), .sel({INSTRS[30], INSTRS[26:25]}));  // open: out2, out5, out6, out7
  Adder #(.width(4)) adder_10 (.a(adder_9_out), .b(multiplier_11_out), .out(adder_10_out));  // open: cin, cout
  assign bit_extender_1_out = {{2{1'b0}}, or_5_out};  // Bit_Extender bit_extender_1
  assign bit_extender_2_out = {{2{1'b0}}, MemRW};  // Bit_Extender bit_extender_2
  assign bit_extender_3_out = {{2{1'b0}}, SB};  // Bit_Extender bit_extender_3
  Adder #(.width(4)) adder_11 (.a(adder_10_out), .b(multiplier_12_out), .out(adder_11_out));  // open: cin, cout
  Multiplier #(.width(3)) multiplier_14 (
    .a(bit_extender_1_out), .b(3'b001), .out(multiplier_14_out));  // open: cin, cout
  Adder #(.width(3)) adder_12 (.a(multiplier_14_out), .b(multiplier_15_out), .out(adder_12_out));  // open: cin, cout
  Multiplier #(.width(3)) multiplier_15 (
    .a(bit_extender_2_out), .b(3'b010), .out(multiplier_15_out));  // open: cin, cout
  Multiplier #(.width(3)) multiplier_16 (
    .a(bit_extender_3_out), .b(3'b011), .out(multiplier_16_out));  // open: cin, cout
  assign bit_extender_4_out = {{2{1'b0}}, U};  // Bit_Extender bit_extender_4
  Multiplier #(.width(3)) multiplier_17 (
    .a(bit_extender_4_out), .b(3'b100), .out(multiplier_17_out));  // open: cin, cout
  assign bit_extender_5_out = {{2{1'b0}}, UJ};  // Bit_Extender bit_extender_5
  Multiplier #(.width(3)) multiplier_18 (
    .a(bit_extender_5_out), .b(3'b101), .out(multiplier_18_out));  // open: cin, cout
  Adder #(.width(4)) adder_13 (.a(adder_11_out), .b(multiplier_13_out), .out(ALUSel));  // open: cin, cout
  Adder #(.width(3)) adder_14 (.a(adder_12_out), .b(multiplier_16_out), .out(adder_14_out));  // open: cin, cout
  Adder #(.width(3)) adder_15 (.a(adder_14_out), .b(multiplier_17_out), .out(adder_15_out));  // open: cin, cout
  Adder #(.width(3)) adder_16 (.a(adder_15_out), .b(multiplier_18_out), .out(ImmSel));  // open: cin, cout
  and and_6 (and_6_out, f3_2, I, f7_0);
  and and_7 (and_7_out, f3_0, R, f7_0);
  and and_8 (and_8_out, f3_0, R, f7_1);
  and and_9 (and_9_out, I, f3_0);
  and and_10 (and_10_out, f3_7, R, f7_0);
  or or_6 (or_6_out, and_10_out, and_11_out);
  and and_11 (and_11_out, f3_7, I, f7_0);
  and and_12 (and_12_out, f3_6, R, f7_0);
  or or_7 (or_7_out, and_12_out, and_13_out);
  and and_13 (and_13_out, f3_6, I, f7_0);
  and and_14 (and_14_out, f3_4, R, f7_0);
  or or_8 (or_8_out, and_14_out, and_15_out);
  and and_15 (and_15_out, f3_4, I, f7_0);
  and and_16 (and_16_out, f3_5, R, f7_0);
  or or_9 (or_9_out, and_16_out, and_17_out);
  and and_17 (and_17_out, f3_5, I, f7_0);
  assign SRA_Sig = {{3{1'b0}}, and_18_out};  // Bit_Extender bit_extender_6
  and and_18 (and_18_out, f3_5, I, f7_0);
  and and_19 (and_19_out, f3_1, R, f7_0);
  or or_10 (or_10_out, and_19_out, and_20_out);
  and and_20 (and_20_out, f3_1, I, f7_0);
  and and_21 (and_21_out, f3_2, R, f7_0);
  or or_11 (or_11_out, and_21_out, and_6_out);
  and and_22 (and_22_out, f3_5, f7_1, R);
  assign DIV_Sig = {{3{1'b0}}, and_22_out};  // Bit_Extender bit_extender_7
  assign REMU_Sig = {{3{1'b0}}, and_23_out};  // Bit_Extender bit_extender_8
  and and_23 (and_23_out, f3_7, f7_1, R);
  and and_24 (and_24_out, f3_0, f7_1, R);
  assign MUL_Sig = {{3{1'b0}}, and_24_out};  // Bit_Extender bit_extender_9
  and and_25 (and_25_out, f3_3, f7_1, R);
  assign MULHU_Sig = {{3{1'b0}}, and_25_out};  // Bit_Extender bit_extender_10
  and and_26 (and_26_out, f3_0, f7_20, R);
  assign SUB_Sig = {{3{1'b0}}, and_26_out};  // Bit_Extender bit_extender_11
  or or_12 (or_12_out, and_7_out, and_8_out, SB, UJ, JALR, WBSel[1], and_9_out, MemRW);
  assign AND_Sig = {{3{1'b0}}, or_6_out};  // Bit_Extender bit_extender_12
  assign OR_Sig = {{3{1'b0}}, or_7_out};  // Bit_Extender bit_extender_13
  assign XOR_Sig = {{3{1'b0}}, or_8_out};  // Bit_Extender bit_extender_14
  assign SRL_Sig = {{3{1'b0}}, or_9_out};  // Bit_Extender bit_extender_15
  assign SLL_Sig = {{3{1'b0}}, or_10_out};  // Bit_Extender bit_extender_16
  assign SLT_Sig = {{3{1'b0}}, or_11_out};  // Bit_Extender bit_extender_17
  assign ADD_Sig = {{3{1'b0}}, or_12_out};  // Bit_Extender bit_extender_18

  // Other names for the same wires on the sheet: Instruction[31:0] = INSTRS; Opcode[4:0] = INSTRS[6:2];
  //   func3[2:0] = INSTRS[14:12]; func7[2:0] = {INSTRS[30], INSTRS[26:25]}; S = MemRW; TERM = out_13; UBLT = BrUn;
  //   ILoad = WBSel[1]
endmodule

module BrComp (
  input  [31:0] RegOut1,
  input  [31:0] RegOut2,
  input  BrUn,
  output BrEq,
  output BrLt
);

  wire comparator_1_lt, comparator_2_lt;

  Comparator #(.width(32)) comparator_1 (.a(RegOut1), .b(RegOut2), .eq(BrEq), .lt(comparator_1_lt));  // open: gt
  Comparator #(.width(32), .mode("unsigned")) comparator_2 (
    .a(RegOut1), .b(RegOut2), .lt(comparator_2_lt));  // open: gt, eq
  Multiplexer #(.enable("false")) multiplexer_1 (.in0(comparator_1_lt), .in1(comparator_2_lt), .out(BrLt), .sel(BrUn));

  // Other names for the same wires on the sheet: Reg1[31:0] = RegOut1; Reg2[31:0] = RegOut2
endmodule

module SelA (
  input  [31:0] PC_Val,
  input  [31:0] RS_1,
  input  ASel_IN,
  output [31:0] SelA_Val
);

  Multiplexer #(.width(32), .enable("false")) multiplexer_1 (.in0(RS_1), .in1(PC_Val), .out(SelA_Val), .sel(ASel_IN));
endmodule

module SelB (
  input  [31:0] Reg2_Val,
  input  [31:0] Imm_Val,
  input  BSel_In,
  output [31:0] SelB_out
);

  Multiplexer #(.width(32), .enable("false")) multiplexer_1 (
    .in0(Reg2_Val), .in1(Imm_Val), .out(SelB_out), .sel(BSel_In));

  // Other names for the same wires on the sheet: RS_2[31:0] = Reg2_Val
endmodule
