// Logisim project regfile.circ as structural Verilog: 1 circuit, main circuit main
module main (
  input  [4:0] rs1,
  input  [4:0] rs2,
  input  [4:0] rd,
  input  [31:0] Write_Data,
  input  RegWEn,
  input  clk,
  input  [31:0] in_7,
  output [31:0] ra,
  output [31:0] sp,
  output [31:0] t0,
  output [31:0] t1,
  output [31:0] t2,
  output [31:0] s0,
  output [31:0] s1,
  output [31:0] a0,
  output [31:0] Read_Data_1,
  output [31:0] Read_Data_2
);

  wire comparator_1_eq, comparator_2_eq, comparator_3_eq, comparator_4_eq, comparator_5_eq, comparator_6_eq,
       comparator_7_eq, comparator_8_eq;
  wire [31:0] multiplexer_1_out, multiplexer_2_out, multiplexer_3_out, multiplexer_4_out, multiplexer_5_out,
       multiplexer_6_out, multiplexer_7_out, multiplexer_8_out;

  Comparator #(.width(5)) comparator_1 (.a(rd), .b(5'b00001), .eq(comparator_1_eq));  // open: gt, lt
  Comparator #(.width(5)) comparator_2 (.a(rd), .b(5'b00010), .eq(comparator_2_eq));  // open: gt, lt
  Comparator #(.width(5)) comparator_3 (.a(rd), .b(5'b00101), .eq(comparator_3_eq));  // open: gt, lt
  Comparator #(.width(5)) comparator_4 (.a(rd), .b(5'b00111), .eq(comparator_4_eq));  // open: gt, lt
  Comparator #(.width(5)) comparator_5 (.a(rd), .b(5'b01000), .eq(comparator_5_eq));  // open: gt, lt
  Comparator #(.width(5)) comparator_6 (.a(rd), .b(5'b01001), .eq(comparator_6_eq));  // open: gt, lt
  Comparator #(.width(5)) comparator_7 (.a(rd), .b(5'b01010), .eq(comparator_7_eq));  // open: gt, lt
  Multiplexer #(.width(32), .enable("false")) multiplexer_1 (
    .in0(ra), .in1(Write_Data), .out(multiplexer_1_out), .sel(comparator_1_eq));
  Multiplexer #(.width(32), .enable("false")) multiplexer_2 (
    .in0(sp), .in1(Write_Data), .out(multiplexer_2_out), .sel(comparator_2_eq));
  Multiplexer #(.width(32), .enable("false")) multiplexer_3 (
    .in0(t0), .in1(Write_Data), .out(multiplexer_3_out), .sel(comparator_3_eq));
  Multiplexer #(.width(32), .enable("false")) multiplexer_4 (
    .in0(t1), .in1(Write_Data), .out(multiplexer_4_out), .sel(comparator_8_eq));
  Comparator #(.width(5)) comparator_8 (.a(rd), .b(5'b00110), .eq(comparator_8_eq));  // open: gt, lt
  Multiplexer #(.width(32), .enable("false")) multiplexer_5 (
    .in0(t2), .in1(Write_Data), .out(multiplexer_5_out), .sel(comparator_4_eq));
  Multiplexer #(.width(32), .enable("false")) multiplexer_6 (
    .in0(s0), .in1(Write_Data), .out(multiplexer_6_out), .sel(comparator_5_eq));
  Multiplexer #(.width(32), .enable("false")) multiplexer_7 (
    .in0(s1), .in1(Write_Data), .out(multiplexer_7_out), .sel(comparator_6_eq));
  Multiplexer #(.width(32), .enable("false")) multiplexer_8 (
    .in0(a0), .in1(Write_Data), .out(multiplexer_8_out), .sel(comparator_7_eq));
  Register #(.width(32)) register_1 (.D(Write_Data), .en(RegWEn), .clk(clk), .Q(in_7), .clr(1'b1));
  Register #(.width(32)) register_2 (.D(multiplexer_1_out), .en(RegWEn), .clk(clk), .Q(ra));  // open: clr
  Register #(.width(32)) register_3 (.D(multiplexer_2_out), .en(RegWEn), .clk(clk), .Q(sp));  // open: clr
  Register #(.width(32)) register_4 (.D(multiplexer_3_out), .en(RegWEn), .clk(clk), .Q(t0));  // open: clr
  Register #(.width(32)) register_5 (.D(multiplexer_4_out), .en(RegWEn), .clk(clk), .Q(t1));  // open: clr
  Register #(.width(32)) register_6 (.D(multiplexer_5_out), .en(RegWEn), .clk(clk), .Q(t2));  // open: clr
  Register #(.width(32)) register_7 (.D(multiplexer_6_out), .en(RegWEn), .clk(clk), .Q(s0));  // open: clr
  Register #(.width(32)) register_8 (.D(multiplexer_7_out), .en(RegWEn), .clk(clk), .Q(s1));  // open: clr
  Register #(.width(32)) register_9 (.D(multiplexer_8_out), .en(RegWEn), .clk(clk), .Q(a0));  // open: clr
  Multiplexer #(.select(5), .width(32), .enable("false")) multiplexer_9 (
    .in0(in_7), .in1(ra), .in2(sp), .in5(t0), .in6(t1), .in7(t2), .in8(s0), .in9(s1), .in10(a0),
    .out(Read_Data_1), .sel(rs1));  // open: in3, in4, in11, in12, in13, in14, in15, in16, in17, in18, in19, in20, in21, in22, in23, in24, in25, in26, in27, in28, in29, in30, in31
  Multiplexer #(.select(5), .width(32), .enable("false")) multiplexer_10 (
    .in0(in_7), .in1(ra), .in2(sp), .in5(t0), .in6(t1), .in7(t2), .in8(s0), .in9(s1), .in10(a0),
    .out(Read_Data_2), .sel(rs2));  // open: in3, in4, in11, in12, in13, in14, in15, in16, in17, in18, in19, in20, in21, in22, in23, in24, in25, in26, in27, in28, in29, in30, in31

  // Other names for the same wires on the sheet: read_data1[31:0] = Read_Data_1; read_data2[31:0] = Read_Data_2;
  //   read_reg1[4:0] = rs1; read_reg2[4:0] = rs2; write_en = RegWEn; write_reg[4:0] = rd; zero[31:0] = in_7

  // Notes on the sheet:
  //   INPUTS to your circuit
  //   DON'T CHANGE THE LOCATIONS OF THE INPUTS AND OUTPUTS!
  //   These are DEBUG/TEST outputs from your circuit.
  //   OUTPUTS from your circuit
endmodule
